# Fritzing sketch SelfLeveling (saved by Fritzing 0.9.2b)
circuit board: 4.95254cm x 4.91051cm
breadboards: 1

parts:
  Part1 = Triple Axis Accelerometer Breakout - ADXL345
  J1 = Basic Servo
  Part2 = Arduino Pro Mini v13
  5V_power = Power plug
  C1 = Electrolytic Capacitor [capacitance=10μF package="0605 [SMD, electrolytic]"]
  C2 = Electrolytic Capacitor [capacitance=100μF package="0807 [SMD, electrolytic]"]
  LD1117 = V_REG_LD1117VXX [package=78xxl]

nets:
  GND: Part1.GND, J1.gnd, Part2.GND, 5V_power.GND, C1.-, C2.-
  N1: Part1.VCC, C1.+, LD1117.OUT
  N2: Part1.CS, Part2.D10_PWM/SS
  N3: Part1.SDO, Part2.D12/MISO
  N4: Part1.SDA, Part2.D11_PWM/MOSI
  N5: Part1.SCL, Part2.D13/SCK
  VCC: J1.vcc, Part2.VCC, 5V_power.VCC, C2.+, LD1117.IN
  N6: J1.pulse, Part2.D3_PWM
